// Logisim project CPU.circ as structural Verilog
module ALU (
  input  [15:0] A,
  input  [15:0] B,
  input  [4:0] shamt,
  input  [5:0] OP,
  output [15:0] OUT,
  output Overflow
);

  wire and_2_out, clock_1_out, comparator_1_lt, n16bit_adder_1_cout, n16bit_adder_2_cout, not_1_out,
       not_2_out, not_3_out;
  wire [15:0] and_1_out, bit_extender_1_out, HIGH_q, LOW_q, multiplexer_1_out, multiplexer_2_out,
       multiplexer_3_out, multiplexer_4_out, multiplexer_5_out, multiplexer_6_out, multiplexer_7_out,
       multiplexer_8_out, multiplier_1_cout, multiplier_1_out, n16bit_adder_1_sum, n16bit_adder_2_sum,
       or_2_out, shifter_1_out, subtractor_1_out;

  or or_1 (Overflow, n16bit_adder_1_cout, n16bit_adder_2_cout);
  _16bit_adder u_16bit_adder_1 (.Sum(n16bit_adder_1_sum), .A(A), .B(B), .Cout(n16bit_adder_1_cout));
  Subtractor #(.width(16)) subtractor_1 (.a(A), .b(B), .out(subtractor_1_out));  // open: bin, bout
  Multiplier #(.width(16)) multiplier_1 (.a(A), .b(B), .out(multiplier_1_out), .cout(multiplier_1_cout));  // open: cin
  assign and_1_out = A & B;  // AND_Gate and_1, 16 bits wide
  assign or_2_out = A | B;  // OR_Gate or_2, 16 bits wide
  _16bit_adder u_16bit_adder_2 (.Sum(n16bit_adder_2_sum), .A(A), .B(B), .Cout(n16bit_adder_2_cout));
  Shifter #(.width(16)) shifter_1 (.in(A), .\dist (shamt[3:0]), .out(shifter_1_out));
  Comparator #(.width(16)) comparator_1 (.a(A), .b(B), .lt(comparator_1_lt));  // open: gt, eq
  assign bit_extender_1_out = {{15{1'b0}}, comparator_1_lt};  // Bit_Extender bit_extender_1
  Register #(.width(16)) LOW (.D(multiplier_1_out), .en(and_2_out), .Q(LOW_q), .clk(clock_1_out));  // open: clr
  Register #(.width(16)) HIGH (.D(multiplier_1_cout), .en(and_2_out), .Q(HIGH_q), .clk(clock_1_out));  // open: clr
  Clock clock_1 (.out(clock_1_out));
  and and_2 (and_2_out, not_1_out, not_2_out, OP[1], not_3_out);
  Multiplexer #(.width(16)) multiplexer_1 (
    .in0(n16bit_adder_1_sum), .in1(subtractor_1_out), .out(multiplexer_1_out), .sel(OP[0]));  // open: en
  Multiplexer #(.width(16)) multiplexer_2 (.in1(and_1_out), .out(multiplexer_2_out), .sel(OP[0]));  // open: in0, en
  Multiplexer #(.width(16)) multiplexer_3 (
    .in0(or_2_out), .in1(n16bit_adder_2_sum), .out(multiplexer_3_out), .sel(OP[0]));  // open: en
  Multiplexer #(.width(16)) multiplexer_4 (
    .in0(shifter_1_out), .in1(bit_extender_1_out), .out(multiplexer_4_out), .sel(OP[0]));  // open: en
  Multiplexer #(.width(16)) multiplexer_5 (
    .in0(HIGH_q), .in1(LOW_q), .out(multiplexer_5_out), .sel(OP[0]));  // open: en
  not not_1 (not_1_out, OP[3]);
  not not_2 (not_2_out, OP[2]);
  not not_3 (not_3_out, OP[0]);
  Multiplexer #(.width(16)) multiplexer_6 (
    .in0(multiplexer_1_out), .in1(multiplexer_2_out), .out(multiplexer_6_out), .sel(OP[1]));  // open: en
  Multiplexer #(.width(16)) multiplexer_7 (
    .in0(multiplexer_6_out), .in1(multiplexer_8_out), .out(multiplexer_7_out), .sel(OP[2]));  // open: en
  Multiplexer #(.width(16)) multiplexer_8 (
    .in0(multiplexer_3_out), .in1(multiplexer_4_out), .out(multiplexer_8_out), .sel(OP[1]));  // open: en
  Multiplexer #(.width(16)) multiplexer_9 (
    .in0(multiplexer_7_out), .in1(multiplexer_5_out), .out(OUT), .sel(OP[3]));  // open: en
endmodule

module full_adder (
  input  A,
  input  B,
  input  Cin,
  output Sum,
  output Cout
);

  wire and_1_out, and_2_out, xor_1_out;

  xor xor_1 (xor_1_out, A, B);
  xor xor_2 (Sum, xor_1_out, Cin);
  and and_1 (and_1_out, Cin, xor_1_out);
  and and_2 (and_2_out, B, A);
  or or_1 (Cout, and_1_out, and_2_out);
endmodule

module register_file (
  input  [4:0] ReadAddress1,
  input  [4:0] ReadAddress2,
  input  [15:0] WriteData,
  input  RegWrite,
  input  [3:0] WriteAddress,
  output [15:0] R1,
  output [15:0] R2
);

  wire demultiplexer_1_out0, demultiplexer_1_out1, demultiplexer_1_out2, demultiplexer_1_out3,
       demultiplexer_1_out4, demultiplexer_1_out5, demultiplexer_1_out6, demultiplexer_1_out7,
       demultiplexer_1_out8, demultiplexer_1_out9, demultiplexer_1_out10, demultiplexer_1_out11,
       demultiplexer_1_out12, demultiplexer_1_out13, demultiplexer_1_out14, demultiplexer_1_out15;
  wire [15:0] _0_q, _1_q, _2_q, _3_q, _4_q, _5_q, _6_q, _7_q, _8_q, _9_q, _10_q, _11_q, _12_q, _13_q, _14_q,
       _15_q;

  Demultiplexer #(.select(4)) demultiplexer_1 (
    .out0(demultiplexer_1_out0), .out1(demultiplexer_1_out1), .out2(demultiplexer_1_out2),
    .out3(demultiplexer_1_out3), .out4(demultiplexer_1_out4), .out5(demultiplexer_1_out5),
    .out6(demultiplexer_1_out6), .out7(demultiplexer_1_out7), .out8(demultiplexer_1_out8),
    .out9(demultiplexer_1_out9), .out10(demultiplexer_1_out10), .out11(demultiplexer_1_out11),
    .out12(demultiplexer_1_out12), .out13(demultiplexer_1_out13), .out14(demultiplexer_1_out14),
    .out15(demultiplexer_1_out15), .in(RegWrite), .sel(WriteAddress));  // open: en
  Register #(.width(16), .trigger("high")) _0 (.D(WriteData), .Q(_0_q), .clk(demultiplexer_1_out0));  // open: en, clr
  Register #(.width(16), .trigger("high")) _4 (.D(WriteData), .Q(_4_q), .clk(demultiplexer_1_out4));  // open: en, clr
  Register #(.width(16), .trigger("high")) _8 (.D(WriteData), .Q(_8_q), .clk(demultiplexer_1_out8));  // open: en, clr
  Register #(.width(16), .trigger("high")) _12 (
    .D(WriteData), .Q(_12_q), .clk(demultiplexer_1_out12));  // open: en, clr
  Register #(.width(16), .trigger("high")) _1 (.D(WriteData), .Q(_1_q), .clk(demultiplexer_1_out1));  // open: en, clr
  Register #(.width(16), .trigger("high")) _5 (.D(WriteData), .Q(_5_q), .clk(demultiplexer_1_out5));  // open: en, clr
  Register #(.width(16), .trigger("high")) _9 (.D(WriteData), .Q(_9_q), .clk(demultiplexer_1_out9));  // open: en, clr
  Register #(.width(16), .trigger("high")) _13 (
    .D(WriteData), .Q(_13_q), .clk(demultiplexer_1_out13));  // open: en, clr
  Register #(.width(16), .trigger("high")) _2 (.D(WriteData), .Q(_2_q), .clk(demultiplexer_1_out2));  // open: en, clr
  Register #(.width(16), .trigger("high")) _6 (.D(WriteData), .Q(_6_q), .clk(demultiplexer_1_out6));  // open: en, clr
  Register #(.width(16), .trigger("high")) _10 (
    .D(WriteData), .Q(_10_q), .clk(demultiplexer_1_out10));  // open: en, clr
  Register #(.width(16), .trigger("high")) _14 (
    .D(WriteData), .Q(_14_q), .clk(demultiplexer_1_out14));  // open: en, clr
  Register #(.width(16), .trigger("high")) _3 (.D(WriteData), .Q(_3_q), .clk(demultiplexer_1_out3));  // open: en, clr
  Register #(.width(16), .trigger("high")) _7 (.D(WriteData), .Q(_7_q), .clk(demultiplexer_1_out7));  // open: en, clr
  Register #(.width(16), .trigger("high")) _11 (
    .D(WriteData), .Q(_11_q), .clk(demultiplexer_1_out11));  // open: en, clr
  Register #(.width(16), .trigger("high")) _15 (
    .D(WriteData), .Q(_15_q), .clk(demultiplexer_1_out15));  // open: en, clr
  Multiplexer #(.select(4), .width(16)) multiplexer_1 (
    .in0(_0_q), .in1(_1_q), .in2(_2_q), .in3(_3_q), .in4(_4_q), .in5(_5_q), .in6(_6_q), .in7(_7_q),
    .in8(_8_q), .in9(_9_q), .in10(_10_q), .in11(_11_q), .in12(_12_q), .in13(_13_q), .in14(_14_q),
    .in15(_15_q), .out(R1), .sel(ReadAddress1[3:0]));  // open: en
  Multiplexer #(.select(4), .width(16)) multiplexer_2 (
    .in0(_0_q), .in1(_1_q), .in2(_2_q), .in3(_3_q), .in4(_4_q), .in5(_5_q), .in6(_6_q), .in7(_7_q),
    .in8(_8_q), .in9(_9_q), .in10(_10_q), .in11(_11_q), .in12(_12_q), .in13(_13_q), .in14(_14_q),
    .in15(_15_q), .out(R2), .sel(ReadAddress2[3:0]));  // open: en
endmodule

module _16bit_adder (
  input  [15:0] A,
  input  [15:0] B,
  output [15:0] Sum,
  output Cout
);

  wire _0_cout, _1_cout, _2_cout, _3_cout, _4_cout, _5_cout, _6_cout, _7_cout, _8_cout, _9_cout, _10_cout,
       _11_cout, _12_cout, _13_cout, _14_cout;

  full_adder _0 (.A(A[0]), .B(B[0]), .Cin(1'b0), .Sum(Sum[0]), .Cout(_0_cout));
  full_adder _4 (.A(A[4]), .B(B[4]), .Cin(_3_cout), .Sum(Sum[4]), .Cout(_4_cout));
  full_adder _8 (.A(A[8]), .B(B[8]), .Cin(_7_cout), .Sum(Sum[8]), .Cout(_8_cout));
  full_adder _12 (.A(A[12]), .B(B[12]), .Cin(_11_cout), .Sum(Sum[12]), .Cout(_12_cout));
  full_adder _1 (.A(A[1]), .B(B[1]), .Cin(_0_cout), .Sum(Sum[1]), .Cout(_1_cout));
  full_adder _5 (.A(A[5]), .B(B[5]), .Cin(_4_cout), .Sum(Sum[5]), .Cout(_5_cout));
  full_adder _9 (.A(A[9]), .B(B[9]), .Cin(_8_cout), .Sum(Sum[9]), .Cout(_9_cout));
  full_adder _13 (.A(A[13]), .B(B[13]), .Cin(_12_cout), .Sum(Sum[13]), .Cout(_13_cout));
  full_adder _2 (.A(A[2]), .B(B[2]), .Cin(_1_cout), .Sum(Sum[2]), .Cout(_2_cout));
  full_adder _6 (.A(A[6]), .B(B[6]), .Cin(_5_cout), .Sum(Sum[6]), .Cout(_6_cout));
  full_adder _10 (.A(A[10]), .B(B[10]), .Cin(_9_cout), .Sum(Sum[10]), .Cout(_10_cout));
  full_adder _14 (.A(A[14]), .B(B[14]), .Cin(_13_cout), .Sum(Sum[14]), .Cout(_14_cout));
  full_adder _3 (.A(A[3]), .B(B[3]), .Cin(_2_cout), .Sum(Sum[3]), .Cout(_3_cout));
  full_adder _7 (.A(A[7]), .B(B[7]), .Cin(_6_cout), .Sum(Sum[7]), .Cout(_7_cout));
  full_adder _11 (.A(A[11]), .B(B[11]), .Cin(_10_cout), .Sum(Sum[11]), .Cout(_11_cout));
  full_adder _15 (.A(A[15]), .B(B[15]), .Cin(_14_cout), .Sum(Sum[15]), .Cout(Cout));
endmodule
